// Logisim project Ejercicio2.circ as structural Verilog: 8 circuits, main circuit main
module main (
  input  Procesar,
  input  [2:0] ABC,
  input  [2:0] DEF,
  input  [2:0] GHI,
  output [2:0] SalidaDeMaquina,
  output [2:0] ResultadoOpcion4,
  output [2:0] ResultadoOpcion6,
  output [2:0] ResultadoOpcion8
);

  wire decoder_1_out0, decoder_1_out1, decoder_1_out2, decoder_1_out3, decoder_1_out4, decoder_1_out5,
       decoder_1_out6, decoder_1_out7, ejercicio3sumador_1_hubocarryflag, ejercicio3sumador_1_overflowflag,
       memoria_interna_1_existepalabravacia, memoria_interna_1_memoriallenadeunos;
  wire [2:0] conversorcomplemento_1_salidaf, ejercicio3sumador_1_result, memoria_interna_1_salida;

  Decoder #(.select(3)) decoder_1 (
    .out0(decoder_1_out0), .out1(decoder_1_out1), .out2(decoder_1_out2), .out3(decoder_1_out3),
    .out4(decoder_1_out4), .out5(decoder_1_out5), .out6(decoder_1_out6), .out7(decoder_1_out7), .sel(ABC),
    .en(Procesar));
  xor xor_1 (ResultadoOpcion6[2], DEF[0], DEF[1], DEF[2], GHI[0], GHI[1], GHI[2]);
  Memoria_Interna memoria_interna_1 (
    .EntradaDatos(GHI), .EscribirAMemoria(decoder_1_out0), .Address(DEF), .ClearMemory(decoder_1_out4),
    .MemoriaLlenaDeUnos(memoria_interna_1_memoriallenadeunos),
    .ExistePalabraVacia(memoria_interna_1_existepalabravacia), .Salida(memoria_interna_1_salida));
  ConversorComplemento conversorcomplemento_1 (
    .EntradaD(DEF[2]), .EntradaE(DEF[1]), .EntradaF(DEF[0]), .SalidaD(conversorcomplemento_1_salidaf[2]),
    .SalidaE(conversorcomplemento_1_salidaf[1]), .SalidaF(conversorcomplemento_1_salidaf[0]));
  Restador2Bits restador2bits_1 (
    .EntradaD(DEF[2]), .EntradaF(DEF[0]), .EntradaE(DEF[1]), .EntradaG(GHI[2]),
    .Resultado1(ResultadoOpcion8[2]), .Overflow(ResultadoOpcion8[0]), .Resultado2(ResultadoOpcion8[1]));
  Ejercicio3Sumador ejercicio3sumador_1 (
    .EntradaGHI(GHI), .EntradaDEF(DEF), .Result(ejercicio3sumador_1_result),
    .HuboCarryFlag(ejercicio3sumador_1_hubocarryflag), .OverflowFlag(ejercicio3sumador_1_overflowflag));
  Ejercicio4 ejercicio4_1 (
    .entradaD(DEF[2]), .entradaE(DEF[1]), .entradaF(DEF[0]), .entradaG(GHI[2]),
    .SalidaEjercicio4(ResultadoOpcion4[2]));
  LED MemoriaLlenaDeUnos (.in(memoria_interna_1_memoriallenadeunos));
  LED ExistePalabraVacia (.in(memoria_interna_1_existepalabravacia));
  LED HuboCarryEnLaSuma (.in(ejercicio3sumador_1_hubocarryflag));
  LED OverflowEnLaSuma (.in(ejercicio3sumador_1_overflowflag));
  LED OverflowEnLaResta (.in(ResultadoOpcion8[0]));
  Multiplexer #(.select(3), .width(3)) multiplexer_1 (
    .in1(memoria_interna_1_salida), .in2(ejercicio3sumador_1_result), .in3(ResultadoOpcion4),
    .in5(ResultadoOpcion6), .in6(conversorcomplemento_1_salidaf), .in7(ResultadoOpcion8),
    .out(SalidaDeMaquina), .sel(ABC));  // open: in0, in4
endmodule

module Memoria_Interna (
  input  [2:0] EntradaDatos,
  input  EscribirAMemoria,
  input  [2:0] Address,
  input  ClearMemory,
  output MemoriaLlenaDeUnos,
  output ExistePalabraVacia,
  output [2:0] Salida
);

  wire and_1_out, and_2_out, and_3_out, and_4_out, and_5_out, and_6_out, and_7_out, and_8_out, and_9_out,
       and_10_out, and_11_out, and_12_out, and_13_out, and_14_out, and_15_out, and_16_out, decoder_1_out0,
       decoder_1_out1, decoder_1_out2, decoder_1_out3, decoder_1_out4, decoder_1_out5, decoder_1_out6,
       decoder_1_out7;
  wire [2:0] d_ff_1_q, d_ff_4_q, d_ff_7_q, d_ff_10_q, d_ff_13_q, d_ff_16_q, d_ff_19_q, d_ff_22_q;

  Decoder #(.select(3)) decoder_1 (
    .out0(decoder_1_out0), .out1(decoder_1_out1), .out2(decoder_1_out2), .out3(decoder_1_out3),
    .out4(decoder_1_out4), .out5(decoder_1_out5), .out6(decoder_1_out6), .out7(decoder_1_out7),
    .sel(Address), .en(EscribirAMemoria));
  Multiplexer #(.select(3), .width(3)) multiplexer_1 (
    .in0(d_ff_1_q), .in1(d_ff_4_q), .in2(d_ff_7_q), .in3(d_ff_10_q), .in4(d_ff_13_q), .in5(d_ff_16_q),
    .in6(d_ff_19_q), .in7(d_ff_22_q), .out(Salida), .sel(Address));
  D_Flip_Flop d_ff_1 (
    .D(EntradaDatos[0]), .clk(decoder_1_out0), .Q(d_ff_1_q[0]), .reset(ClearMemory));  // open: Qn, preset
  D_Flip_Flop d_ff_2 (
    .D(EntradaDatos[1]), .clk(decoder_1_out0), .Q(d_ff_1_q[1]), .reset(ClearMemory));  // open: Qn, preset
  D_Flip_Flop d_ff_3 (
    .D(EntradaDatos[2]), .clk(decoder_1_out0), .Q(d_ff_1_q[2]), .reset(ClearMemory));  // open: Qn, preset
  and and_1 (and_1_out, d_ff_1_q[0], d_ff_1_q[1], d_ff_1_q[2]);
  D_Flip_Flop d_ff_4 (
    .D(EntradaDatos[0]), .clk(decoder_1_out1), .Q(d_ff_4_q[0]), .reset(ClearMemory));  // open: Qn, preset
  D_Flip_Flop d_ff_5 (
    .D(EntradaDatos[1]), .clk(decoder_1_out1), .Q(d_ff_4_q[1]), .reset(ClearMemory));  // open: Qn, preset
  D_Flip_Flop d_ff_6 (
    .D(EntradaDatos[2]), .clk(decoder_1_out1), .Q(d_ff_4_q[2]), .reset(ClearMemory));  // open: Qn, preset
  and and_2 (and_2_out, ~d_ff_1_q[0], ~d_ff_1_q[1], ~d_ff_1_q[2]);  // AND_Gate
  and and_3 (and_3_out, d_ff_4_q[0], d_ff_4_q[1], d_ff_4_q[2]);
  D_Flip_Flop d_ff_7 (
    .D(EntradaDatos[0]), .clk(decoder_1_out2), .Q(d_ff_7_q[0]), .reset(ClearMemory));  // open: Qn, preset
  D_Flip_Flop d_ff_8 (
    .D(EntradaDatos[1]), .clk(decoder_1_out2), .Q(d_ff_7_q[1]), .reset(ClearMemory));  // open: Qn, preset
  D_Flip_Flop d_ff_9 (
    .D(EntradaDatos[2]), .clk(decoder_1_out2), .Q(d_ff_7_q[2]), .reset(ClearMemory));  // open: Qn, preset
  and and_4 (and_4_out, ~d_ff_4_q[0], ~d_ff_4_q[1], ~d_ff_4_q[2]);  // AND_Gate
  and and_5 (and_5_out, d_ff_7_q[0], d_ff_7_q[1], d_ff_7_q[2]);
  and and_6 (and_6_out, ~d_ff_7_q[0], ~d_ff_7_q[1], ~d_ff_7_q[2]);  // AND_Gate
  D_Flip_Flop d_ff_10 (
    .D(EntradaDatos[0]), .clk(decoder_1_out3), .Q(d_ff_10_q[0]), .reset(ClearMemory));  // open: Qn, preset
  D_Flip_Flop d_ff_11 (
    .D(EntradaDatos[1]), .clk(decoder_1_out3), .Q(d_ff_10_q[1]), .reset(ClearMemory));  // open: Qn, preset
  D_Flip_Flop d_ff_12 (
    .D(EntradaDatos[2]), .clk(decoder_1_out3), .Q(d_ff_10_q[2]), .reset(ClearMemory));  // open: Qn, preset
  and and_7 (and_7_out, d_ff_10_q[0], d_ff_10_q[1], d_ff_10_q[2]);
  and and_8 (and_8_out, ~d_ff_10_q[0], ~d_ff_10_q[1], ~d_ff_10_q[2]);  // AND_Gate
  D_Flip_Flop d_ff_13 (
    .D(EntradaDatos[0]), .clk(decoder_1_out4), .Q(d_ff_13_q[0]), .reset(ClearMemory));  // open: Qn, preset
  D_Flip_Flop d_ff_14 (
    .D(EntradaDatos[1]), .clk(decoder_1_out4), .Q(d_ff_13_q[1]), .reset(ClearMemory));  // open: Qn, preset
  D_Flip_Flop d_ff_15 (
    .D(EntradaDatos[2]), .clk(decoder_1_out4), .Q(d_ff_13_q[2]), .reset(ClearMemory));  // open: Qn, preset
  and and_9 (and_9_out, d_ff_13_q[0], d_ff_13_q[1], d_ff_13_q[2]);
  and and_10 (and_10_out, ~d_ff_13_q[0], ~d_ff_13_q[1], ~d_ff_13_q[2]);  // AND_Gate
  D_Flip_Flop d_ff_16 (
    .D(EntradaDatos[0]), .clk(decoder_1_out5), .Q(d_ff_16_q[0]), .reset(ClearMemory));  // open: Qn, preset
  D_Flip_Flop d_ff_17 (
    .D(EntradaDatos[1]), .clk(decoder_1_out5), .Q(d_ff_16_q[1]), .reset(ClearMemory));  // open: Qn, preset
  D_Flip_Flop d_ff_18 (
    .D(EntradaDatos[2]), .clk(decoder_1_out5), .Q(d_ff_16_q[2]), .reset(ClearMemory));  // open: Qn, preset
  and and_11 (and_11_out, d_ff_16_q[0], d_ff_16_q[1], d_ff_16_q[2]);
  and and_12 (and_12_out, ~d_ff_16_q[0], ~d_ff_16_q[1], ~d_ff_16_q[2]);  // AND_Gate
  D_Flip_Flop d_ff_19 (
    .D(EntradaDatos[0]), .clk(decoder_1_out6), .Q(d_ff_19_q[0]), .reset(ClearMemory));  // open: Qn, preset
  D_Flip_Flop d_ff_20 (
    .D(EntradaDatos[1]), .clk(decoder_1_out6), .Q(d_ff_19_q[1]), .reset(ClearMemory));  // open: Qn, preset
  D_Flip_Flop d_ff_21 (
    .D(EntradaDatos[2]), .clk(decoder_1_out6), .Q(d_ff_19_q[2]), .reset(ClearMemory));  // open: Qn, preset
  and and_13 (and_13_out, d_ff_19_q[0], d_ff_19_q[1], d_ff_19_q[2]);
  and and_14 (and_14_out, ~d_ff_19_q[0], ~d_ff_19_q[1], ~d_ff_19_q[2]);  // AND_Gate
  D_Flip_Flop d_ff_22 (
    .D(EntradaDatos[0]), .clk(decoder_1_out7), .Q(d_ff_22_q[0]), .reset(ClearMemory));  // open: Qn, preset
  D_Flip_Flop d_ff_23 (
    .D(EntradaDatos[1]), .clk(decoder_1_out7), .Q(d_ff_22_q[1]), .reset(ClearMemory));  // open: Qn, preset
  D_Flip_Flop d_ff_24 (
    .D(EntradaDatos[2]), .clk(decoder_1_out7), .Q(d_ff_22_q[2]), .reset(ClearMemory));  // open: Qn, preset
  and and_15 (and_15_out, d_ff_22_q[0], d_ff_22_q[1], d_ff_22_q[2]);
  and and_16 (and_16_out, ~d_ff_22_q[0], ~d_ff_22_q[1], ~d_ff_22_q[2]);  // AND_Gate
  and and_17 (MemoriaLlenaDeUnos, and_1_out, and_3_out, and_5_out, and_7_out, and_9_out, and_11_out, and_13_out, and_15_out);
  or or_1 (ExistePalabraVacia, and_2_out, and_4_out, and_6_out, and_8_out, and_10_out, and_12_out, and_14_out, and_16_out);
endmodule

module Ejercicio3Sumador (
  input  [2:0] EntradaGHI,
  input  [2:0] EntradaDEF,
  output [2:0] Result,
  output HuboCarryFlag,
  output OverflowFlag
);

  wire sumador1bit_1_cout, sumador1bit_2_cout;

  Sumador1Bit sumador1bit_1 (
    .A(EntradaGHI[0]), .B(EntradaDEF[0]), .Salida(Result[0]), .Cout(sumador1bit_1_cout));  // open: Cin
  Sumador1Bit sumador1bit_2 (
    .A(EntradaGHI[1]), .B(EntradaDEF[1]), .Cin(sumador1bit_1_cout), .Salida(Result[1]),
    .Cout(sumador1bit_2_cout));
  Sumador1Bit sumador1bit_3 (
    .A(EntradaGHI[2]), .B(EntradaDEF[2]), .Cin(sumador1bit_2_cout), .Salida(Result[2]), .Cout(OverflowFlag));
  or or_1 (HuboCarryFlag, sumador1bit_1_cout, sumador1bit_2_cout);
endmodule

module Sumador1Bit (
  input  A,
  input  B,
  input  Cin,
  output Salida,
  output Cout
);

  wire and_1_out, and_2_out, and_3_out;

  xor xor_1 (Salida, A, B, Cin);
  and and_1 (and_1_out, A, Cin);
  and and_2 (and_2_out, A, B);
  and and_3 (and_3_out, B, Cin);
  or or_1 (Cout, and_1_out, and_2_out, and_3_out);
endmodule

module ConversorComplemento (
  input  EntradaD,
  input  EntradaE,
  input  EntradaF,
  output SalidaD,
  output SalidaE,
  output SalidaF
);

  wire and_1_out, and_2_out, and_3_out, and_4_out, and_5_out, not_1_out, not_2_out, not_3_out;

  not not_1 (not_1_out, EntradaD);
  not not_2 (not_2_out, EntradaE);
  not not_3 (not_3_out, EntradaF);
  and and_1 (and_1_out, not_1_out, EntradaF);
  and and_2 (and_2_out, not_1_out, EntradaE);
  and and_3 (and_3_out, EntradaD, not_2_out, not_3_out);
  and and_4 (and_4_out, not_2_out, EntradaF);
  and and_5 (and_5_out, EntradaE, not_3_out);
  or or_1 (SalidaD, and_1_out, and_2_out, and_3_out);
  or or_2 (SalidaE, and_4_out, and_5_out);

  assign SalidaF = EntradaF;
endmodule

module Ejercicio4 (
  input  entradaD,
  input  entradaE,
  input  entradaF,
  input  entradaG,
  output SalidaEjercicio4
);

  wire and_1_out, and_2_out, and_3_out, and_4_out;

  and and_1 (and_1_out, entradaD, entradaE, entradaF);
  and and_2 (and_2_out, entradaD, ~entradaE, ~entradaF, entradaG);  // AND_Gate
  and and_3 (and_3_out, ~entradaD, ~entradaE, ~entradaF, ~entradaG);  // AND_Gate
  and and_4 (and_4_out, entradaE, entradaF, ~entradaG);  // AND_Gate
  or or_1 (SalidaEjercicio4, and_1_out, and_2_out, and_3_out, and_4_out);
endmodule

module Restador1Bit (
  input  A,
  input  B,
  input  Cin,
  output Resultado,
  output Cout
);

  wire and_1_out, and_2_out, and_3_out;

  xor xor_1 (Resultado, B, Cin, A);
  and and_1 (and_1_out, ~A, B);  // AND_Gate
  and and_2 (and_2_out, ~A, Cin);  // AND_Gate
  and and_3 (and_3_out, B, Cin);
  or or_1 (Cout, and_1_out, and_2_out, and_3_out);
endmodule

module Restador2Bits (
  input  EntradaD,
  input  EntradaF,
  input  EntradaE,
  input  EntradaG,
  output Resultado1,
  output Overflow,
  output Resultado2
);

  wire restador1bit_2_cout;

  Restador1Bit restador1bit_1 (
    .A(EntradaD), .B(EntradaF), .Cin(restador1bit_2_cout), .Resultado(Resultado1), .Cout(Overflow));
  Restador1Bit restador1bit_2 (
    .A(EntradaE), .B(EntradaG), .Resultado(Resultado2), .Cout(restador1bit_2_cout));  // open: Cin
endmodule
